# Fritzing sketch PatrolScoutsFritzing (saved by Fritzing 0.9.3b)

parts:
  Mod1 = Raspberry Pi 4B  # not connected
  IC1 = Rasberry Pi NIOR Camera [chip_label=IC package="DIP (Dual Inline) [THT]"]  # not connected
  920KV_Motor1 = DJI 920 KV Motor
  M1 = ESC
  920KV_Motor2 = DJI 920 KV Motor
  M2 = ESC
  920KV_Motor3 = DJI 920 KV Motor
  M3 = ESC
  920KV_Motor4 = DJI 920 KV Motor
  M4 = ESC
  U1 = LIPO-2000mAh [package=lipo-2000]
  U2 = Voltage Regulator [package=sot223]
  U3 = LIPO-2000mAh [package=lipo-2000]
  U4 = Voltage Regulator [package=sot223]
  J1 = Piezo Speaker  # not connected
  ANT1 = Antenna  # not connected
  U5 = SUP500F [package=sup500f]  # not connected
  S1 = SPST Switch [package=switch-spdt_kit]  # not connected
  SONAR1 = Maxbotix MaxSonar Ultrasonic Sensor  # not connected

nets:
  N1: 920KV_Motor1.w, M1.W
  N2: 920KV_Motor1.v, M1.V
  N3: 920KV_Motor1.u, M1.U
  N4: 920KV_Motor2.w, M2.W
  N5: 920KV_Motor2.v, M2.V
  N6: 920KV_Motor2.u, M2.U
  N7: 920KV_Motor3.w, M3.W
  N8: 920KV_Motor3.v, M3.V
  N9: 920KV_Motor3.u, M3.U
  N10: 920KV_Motor4.w, M4.W
  N11: 920KV_Motor4.v, M4.V
  N12: 920KV_Motor4.u, M4.U
  N13: U1.+, U2.ADJ
  N14: U1.-, U2.OUT
  N15: U3.+, U4.ADJ
  N16: U3.-, U4.OUT

notes:
  Pi Camera Module V3
  920kV Brushless Motor
  Power Distribution
  Board
  DC-DC Module
  11.1V
  30C LI-PO
  5300mAh
  3.7V
  LI-IO
  4500mAh
  Telemetry Module
  Saftery Switch
  Buzzer
  GPS Module
  MB1430 Rangefinder

custom parts:
  Rasberry Pi NIOR Camera: Camera
  DJI 920 KV Motor: DJI Brushless Outrunner 2212/920K Motor F330-550
  Maxbotix MaxSonar Ultrasonic Sensor: Maxbotix MaxSonar Ultrasonic Sensor LV-EZ0, LV-EZ1, LV-EZ2, LV-EZ3, LV-EZ4
